# Fritzing sketch S0Sensor (saved by Fritzing 0.8.7b)
perfboards: 1

parts:
  Bauteil1 = Arduino Nano (Rev3.0)
  J1 = Screw terminal - 2 pins [package=THT]  # not connected
  J4 = Screw terminal - 2 pins [package=THT]  # not connected
  LED1 = LED - 5mm [color="Red (633nm)" package="5 mm [THT]"]
  R1 = Resistor [tolerance=±5% resistance=220 package=THT]
  RHT1 = Humidity and Temperature Sensor RHT03
  J2 = Screw terminal - 2 pins [package=THT]  # not connected
  J3 = Screw terminal - 2 pins [package=THT]  # not connected

nets:
  N1: Bauteil1.D6, RHT1.Vcc
  N2: Bauteil1.D7, LED1.anode
  N3: LED1.cathode, R1.Pin_1

notes:
  DHT22
